# Fritzing sketch labrack_raspi_arduino_current_sink (saved by Fritzing 0.9.2b)
circuit board: 7.5cm x 12.4cm
breadboards: 1

parts:
  C4 = Ceramic Capacitor [capacitance=22nF package="200 mil [THT, multilayer]"]
  Part1 = Arduino Pro Mini v13
  ad780 = DIP - 8 pins [chip_label=IC package="DIP (Dual Inline) [THT]"]
  C6 = Ceramic Capacitor [capacitance=10µF package="200 mil [THT, multilayer]"]
  R12 = Resistor [tolerance=±5% resistance=10k package=THT]
  R11 = Resistor [tolerance=±5% resistance=1M package=THT]
  PWM = Resistor [tolerance=±5% resistance=270 package=THT]
  R9 = Resistor [tolerance=±5% resistance=2.2k package=THT]
  R10 = Resistor [tolerance=±5% resistance=10k package=THT]
  C1 = Electrolytic Capacitor [capacitance=1000µF package="300 mil [THT, electrolytic]"]
  lm324n = DIP - 14 pins [chip_label=IC package="DIP (Dual Inline) [THT]"]
  C2 = Ceramic Capacitor [capacitance=100nF package="200 mil [THT, multilayer]"]
  R7 = Resistor [tolerance=±5% resistance=150 package=THT]
  R6 = Resistor [tolerance=±5% resistance=2.2k package=THT]
  Q3 = MOSFET-NCHANNEL [package=to220v]
  PWM_2 = Resistor [tolerance=±5% resistance=1k package=THT]
  R13 = TRIMPOT [package=trim_pot_pth]
  R14 = Resistor [tolerance=±5% resistance=1M package=THT]
  C5 = Ceramic Capacitor [capacitance=100nF package="200 mil [THT, multilayer]"]
  +15 = Screw terminal - 2 pins [package=THT]
  U2 = SIP - 5 pins [chip_label=IC package="SIP (Single Inline) [THT]"]
  U3 = Voltage Regulator [package=to-92]
  U4 = Voltage Regulator [package=to-92]
  J1 = female pin header, 2 pins [form="♀ (female)"]
  +16 = Screw terminal - 2 pins [package=THT]

nets (from the pcb view):
  N1: C4.0, R6.Pin_0
  N2: C4.1, lm324n.output_1, R7.Pin_0
  VIN: Part1.RAW, ad780.VIN, C5.1, U2.VCC, U3.OUT
  GND: Part1.GND, ad780.GND, ad780.2.5v_/_3.0v, C6.1, R12.Pin_1, PWM.Pin_0, R10.Pin_1, C1.-, lm324n.vcc-, C2.0, R13.CCW, C5.0, +15.pin2, U2.GND, J1.pin2
  N3: Part1.A2, R12.Pin_0, R11.Pin_0
  N4: Part1.A0, R9.Pin_0, R10.Pin_0
  N5: Part1.D3_PWM, PWM_2.Pin_0
  N6: ad780.TRIM, R14.Pin_1
  N7: ad780.VOUT, C6.0, R13.CW
  N8: R11.Pin_1, Q3.D, +16.pin1
  N9: PWM.Pin_1, C1.+, lm324n.non-inverting_input_1, PWM_2.Pin_1
  N10: R9.Pin_1, U2.OUT
  N11: lm324n.inverting_input_1, R6.Pin_1, Q3.S
  N12: lm324n.vcc+, C2.1, +15.pin1, U3.IN, U4.IN
  N13: R7.Pin_1, Q3.G
  N14: R13.WIPER, R14.Pin_0
  N15: U2.CURRENT#3, +16.pin2
  N16: U4.OUT, J1.pin1

custom parts:
  DIP - 8 pins: A DIP stand-in part for whatever IC you want. With 8 pins on a 300mil dual inline package (DIP) footprint.
  DIP - 14 pins: A DIP stand-in part for whatever IC you want. With 14 pins on a 300mil dual inline package (DIP) footprint.
  SIP - 5 pins: A SIP stand-in part for whatever you want. With 5 pins on a 300 mil single inline package (SIP) footprint.
